# Fritzing sketch Turtle_Cnt (saved by Fritzing 0.9.2b)
breadboards: 1

parts:
  Componente1 = Arduino Uno (Rev3)
  S1 = Pushbutton [package="[THT]"]
  S2 = Pushbutton [package="[THT]"]
  S3 = Pushbutton [package="[THT]"]
  S4 = Pushbutton [package="[THT]"]
  R1 = Resistor [tolerance=±5% resistance=10k package=THT]
  R2 = Resistor [tolerance=±5% resistance=10k package=THT]
  R3 = Resistor [tolerance=±5% resistance=10k package=THT]
  R4 = Resistor [tolerance=±5% resistance=10k package=THT]
  U1 = LCD-16X2 [package=lcd-16x2]
  R5 = Resistor [tolerance=±5% resistance=220 package=THT]

nets:
  N1: Componente1.D8, S2.Pin_1, S2.Pin_2, R3.Pin_0
  N2: Componente1.D10_PWM/SS, S1.Pin_1, S1.Pin_2, R2.Pin_0
  N3: Componente1.D11_PWM/MOSI, U1.E
  N4: Componente1.D12/MISO, U1.RS
  N5: Componente1.D2, U1.DB7
  N6: Componente1.D3_PWM, U1.DB6
  N7: Componente1.D4, U1.DB5
  N8: Componente1.D5_PWM, U1.DB4
  N9: Componente1.D6_PWM, S3.Pin_1, S3.Pin_2, R1.Pin_0
  N10: Componente1.D7, S4.Pin_1, S4.Pin_2, R4.Pin_0
  N11: S1.Pin_3, S1.Pin_4, S2.Pin_3, S2.Pin_4, S3.Pin_3, S3.Pin_4, S4.Pin_3, S4.Pin_4
  N12: R1.Pin_1, R2.Pin_1, R3.Pin_1, R4.Pin_1
  N13: U1.VSS, U1.VO, U1.R_W, U1.K
  N14: U1.VDD, R5.Pin_0
  N15: U1.A, R5.Pin_1
